# Fritzing sketch pcb (saved by Fritzing 0.9.3b)
circuit board: 5.86649cm x 3.10617cm
breadboards: 1
perfboards: 1

parts:
  IC1 = H-Bridge [package=THT]
  VCC1 = Battery block 9V
  IC2 = H-Bridge [package=THT]
  VCC2 = Battery block 9V

nets:
  N1: IC1.1_2EN, IC1.3_4EN
  GND1: IC1.GND1, IC1.GND2, IC1.GND3, IC1.GND4, VCC1.-
  N2: IC1.VCC2, VCC1.+
  GND1_2: IC2.GND1, IC2.GND2, IC2.GND3, IC2.GND4, VCC2.-
  N3: IC2.VCC2, VCC2.+
